// Logisim project comp2_completo.circ as structural Verilog: 10 circuits, main circuit main
module main (
  input  [7:0] in_1,
  input  [7:0] in_2,
  input  [7:0] in_3,
  input  [7:0] in_4,
  input  [7:0] in_5,
  input  [7:0] in_6,
  input  [7:0] in_7,
  input  [7:0] in_8,
  output [7:0] out_9,
  output [7:0] out_10,
  output [7:0] out_11,
  output [7:0] out_12,
  output [7:0] out_13,
  output [7:0] out_14,
  output [7:0] out_15,
  output [7:0] out_16
);

  ordenador_completo ordenador_completo_1 (
    .I0(in_1), .I1(in_2), .I2(in_3), .I3(in_4), .I4(in_5), .I5(in_6), .I6(in_7), .I7(in_8), .S0(out_9),
    .S1(out_10), .S2(out_11), .S3(out_12), .S4(out_13), .S5(out_14), .S6(out_15), .S7(out_16));

  // Notes on the sheet:
  //   RED DE ORDENAMIENTO PARA NÚMEROS BINARIOS DE 8 BITS
endmodule

module comparador_basico (
  input  A,
  input  B,
  output AMB,
  output AIB,
  output AMeB
);

  wire and_2_out, and_3_out, not_1_out, not_2_out;

  not not_1 (not_1_out, B);
  and and_1 (AMB, A, not_1_out);
  not not_2 (not_2_out, A);
  and and_2 (and_2_out, not_2_out, not_1_out);
  and and_3 (and_3_out, A, B);
  and and_4 (AMeB, not_2_out, B);
  or or_1 (AIB, and_2_out, and_3_out);
endmodule

module comparador_A2 (
  input  [7:0] A,
  input  [7:0] B,
  output AMB,
  output AIB,
  output AMeB
);

  wire comparador_cascada_1_aib, comparador_cascada_1_amb, comparador_cascada_1_ameb,
       comparador_cascada_2_aib, comparador_cascada_2_amb, comparador_cascada_2_ameb,
       comparador_cascada_3_aib, comparador_cascada_3_amb, comparador_cascada_3_ameb,
       comparador_cascada_4_aib, comparador_cascada_4_amb, comparador_cascada_4_ameb,
       comparador_cascada_5_aib, comparador_cascada_5_amb, comparador_cascada_5_ameb,
       comparador_cascada_6_aib, comparador_cascada_6_amb, comparador_cascada_6_ameb,
       comparador_cascada_7_aib, comparador_cascada_7_amb, comparador_cascada_7_ameb;

  comparador_cascada comparador_cascada_1 (
    .A(A[0]), .B(B[0]), .PAMB(1'b0), .PAIB(1'b1), .PAMeB(1'b0), .AMB(comparador_cascada_1_amb),
    .AIB(comparador_cascada_1_aib), .AMeB(comparador_cascada_1_ameb));
  comparador_cascada comparador_cascada_2 (
    .A(A[1]), .B(B[1]), .PAMB(comparador_cascada_1_amb), .PAIB(comparador_cascada_1_aib),
    .PAMeB(comparador_cascada_1_ameb), .AMB(comparador_cascada_2_amb), .AIB(comparador_cascada_2_aib),
    .AMeB(comparador_cascada_2_ameb));
  comparador_cascada comparador_cascada_3 (
    .A(A[2]), .B(B[2]), .PAMB(comparador_cascada_2_amb), .PAIB(comparador_cascada_2_aib),
    .PAMeB(comparador_cascada_2_ameb), .AMB(comparador_cascada_3_amb), .AIB(comparador_cascada_3_aib),
    .AMeB(comparador_cascada_3_ameb));
  comparador_cascada comparador_cascada_4 (
    .A(A[3]), .B(B[3]), .PAMB(comparador_cascada_3_amb), .PAIB(comparador_cascada_3_aib),
    .PAMeB(comparador_cascada_3_ameb), .AMB(comparador_cascada_4_amb), .AIB(comparador_cascada_4_aib),
    .AMeB(comparador_cascada_4_ameb));
  comparador_cascada comparador_cascada_5 (
    .A(A[4]), .B(B[4]), .PAMB(comparador_cascada_4_amb), .PAIB(comparador_cascada_4_aib),
    .PAMeB(comparador_cascada_4_ameb), .AMB(comparador_cascada_5_amb), .AIB(comparador_cascada_5_aib),
    .AMeB(comparador_cascada_5_ameb));
  comparador_cascada comparador_cascada_6 (
    .A(A[5]), .B(B[5]), .PAMB(comparador_cascada_5_amb), .PAIB(comparador_cascada_5_aib),
    .PAMeB(comparador_cascada_5_ameb), .AMB(comparador_cascada_6_amb), .AIB(comparador_cascada_6_aib),
    .AMeB(comparador_cascada_6_ameb));
  comparador_cascada comparador_cascada_7 (
    .A(A[6]), .B(B[6]), .PAMB(comparador_cascada_6_amb), .PAIB(comparador_cascada_6_aib),
    .PAMeB(comparador_cascada_6_ameb), .AMB(comparador_cascada_7_amb), .AIB(comparador_cascada_7_aib),
    .AMeB(comparador_cascada_7_ameb));
  comparador_cascada comparador_cascada_8 (
    .A(B[7]), .B(A[7]), .PAMB(comparador_cascada_7_amb), .PAIB(comparador_cascada_7_aib),
    .PAMeB(comparador_cascada_7_ameb), .AMB(AMB), .AIB(AIB), .AMeB(AMeB));
endmodule

module comparador_cascada (
  input  A,
  input  B,
  input  PAMB,
  input  PAIB,
  input  PAMeB,
  output AMB,
  output AIB,
  output AMeB
);

  wire and_1_out, and_3_out, comparador_basico_1_aib, comparador_basico_1_amb, comparador_basico_1_ameb;

  comparador_basico comparador_basico_1 (
    .A(A), .B(B), .AMB(comparador_basico_1_amb), .AIB(comparador_basico_1_aib),
    .AMeB(comparador_basico_1_ameb));
  and and_1 (and_1_out, comparador_basico_1_aib, PAMB);
  or or_1 (AMB, comparador_basico_1_amb, and_1_out);
  and and_2 (AIB, comparador_basico_1_aib, PAIB);
  or or_2 (AMeB, comparador_basico_1_ameb, and_3_out);
  and and_3 (and_3_out, comparador_basico_1_aib, PAMeB);
endmodule

module ordenador (
  input  [7:0] A,
  input  [7:0] B,
  output [7:0] out_3,
  output [7:0] out_4
);

  wire comparador_a2_1_aib, comparador_a2_1_amb, comparador_a2_1_ameb, or_1_out;

  comparador_A2 comparador_a2_1 (
    .A(A), .B(B), .AMB(comparador_a2_1_amb), .AIB(comparador_a2_1_aib), .AMeB(comparador_a2_1_ameb));
  or or_1 (or_1_out, comparador_a2_1_amb, comparador_a2_1_aib);
  mux_ocho mux (.S(or_1_out), .Y(out_3), .I(B), .O(A));
  mux_ocho mux_ocho_1 (.S(or_1_out), .Y(out_4), .I(A), .O(B));
  // also tied to GND on the sheet: comparador_a2_1_ameb
endmodule

module ordenador_completo (
  input  [7:0] I0,
  input  [7:0] I1,
  input  [7:0] I2,
  input  [7:0] I3,
  input  [7:0] I4,
  input  [7:0] I5,
  input  [7:0] I6,
  input  [7:0] I7,
  output [7:0] S0,
  output [7:0] S1,
  output [7:0] S2,
  output [7:0] S3,
  output [7:0] S4,
  output [7:0] S5,
  output [7:0] S6,
  output [7:0] S7
);

  wire [7:0] ordenador_1_out_3, ordenador_1_out_4, ordenador_2_out_3, ordenador_2_out_4, ordenador_3_out_3,
       ordenador_3_out_4, ordenador_4_out_3, ordenador_4_out_4, ordenador_5_out_3, ordenador_5_out_4,
       ordenador_6_out_3, ordenador_6_out_4, ordenador_7_out_3, ordenador_7_out_4, ordenador_8_out_3,
       ordenador_8_out_4, ordenador_9_out_4, ordenador_10_out_3, ordenador_11_out_3, ordenador_11_out_4,
       ordenador_12_out_3, ordenador_12_out_4, ordenador_13_out_3, ordenador_13_out_4, ordenador_14_out_4,
       ordenador_15_out_3, ordenador_15_out_4, ordenador_16_out_3, ordenador_17_out_3, ordenador_17_out_4,
       ordenador_18_out_3, ordenador_18_out_4, ordenador_19_out_4, ordenador_20_out_3;

  ordenador ordenador_1 (.A(I0), .B(I1), .out_3(ordenador_1_out_3), .out_4(ordenador_1_out_4));
  ordenador ordenador_2 (.A(I2), .B(I3), .out_3(ordenador_2_out_3), .out_4(ordenador_2_out_4));
  ordenador ordenador_3 (.A(I4), .B(I5), .out_3(ordenador_3_out_3), .out_4(ordenador_3_out_4));
  ordenador ordenador_4 (.A(I6), .B(I7), .out_3(ordenador_4_out_3), .out_4(ordenador_4_out_4));
  ordenador ordenador_5 (
    .A(ordenador_1_out_3), .B(ordenador_2_out_3), .out_3(ordenador_5_out_3), .out_4(ordenador_5_out_4));
  ordenador ordenador_6 (
    .A(ordenador_1_out_4), .B(ordenador_2_out_4), .out_3(ordenador_6_out_3), .out_4(ordenador_6_out_4));
  ordenador ordenador_7 (
    .A(ordenador_3_out_3), .B(ordenador_4_out_3), .out_3(ordenador_7_out_3), .out_4(ordenador_7_out_4));
  ordenador ordenador_8 (
    .A(ordenador_3_out_4), .B(ordenador_4_out_4), .out_3(ordenador_8_out_3), .out_4(ordenador_8_out_4));
  ordenador ordenador_9 (.A(ordenador_5_out_3), .B(ordenador_7_out_3), .out_3(S0), .out_4(ordenador_9_out_4));
  ordenador ordenador_10 (.A(ordenador_6_out_4), .B(ordenador_8_out_4), .out_3(ordenador_10_out_3), .out_4(S7));
  ordenador ordenador_11 (
    .A(ordenador_9_out_4), .B(ordenador_5_out_4), .out_3(ordenador_11_out_3), .out_4(ordenador_11_out_4));
  ordenador ordenador_12 (
    .A(ordenador_6_out_3), .B(ordenador_7_out_4), .out_3(ordenador_12_out_3), .out_4(ordenador_12_out_4));
  ordenador ordenador_13 (
    .A(ordenador_8_out_3), .B(ordenador_10_out_3), .out_3(ordenador_13_out_3), .out_4(ordenador_13_out_4));
  ordenador ordenador_14 (.A(ordenador_11_out_3), .B(ordenador_12_out_3), .out_3(S1), .out_4(ordenador_14_out_4));
  ordenador ordenador_15 (
    .A(ordenador_11_out_4), .B(ordenador_12_out_4), .out_3(ordenador_15_out_3), .out_4(ordenador_15_out_4));
  ordenador ordenador_16 (.A(ordenador_15_out_4), .B(ordenador_13_out_4), .out_3(ordenador_16_out_3), .out_4(S6));
  ordenador ordenador_17 (
    .A(ordenador_14_out_4), .B(ordenador_13_out_3), .out_3(ordenador_17_out_3), .out_4(ordenador_17_out_4));
  ordenador ordenador_18 (
    .A(ordenador_15_out_3), .B(ordenador_16_out_3), .out_3(ordenador_18_out_3), .out_4(ordenador_18_out_4));
  ordenador ordenador_19 (.A(ordenador_17_out_3), .B(ordenador_18_out_3), .out_3(S2), .out_4(ordenador_19_out_4));
  ordenador ordenador_20 (.A(ordenador_17_out_4), .B(ordenador_18_out_4), .out_3(ordenador_20_out_3), .out_4(S5));
  ordenador ordenador_21 (.A(ordenador_19_out_4), .B(ordenador_20_out_3), .out_3(S3), .out_4(S4));

  // Notes on the sheet:
  //   Menores3-4
endmodule

module mux (
  input  S,
  input  O,
  input  I,
  output Y
);

  wire and_1_out, and_2_out, not_1_out;

  not not_1 (not_1_out, S);
  and and_1 (and_1_out, O, not_1_out);
  and and_2 (and_2_out, I, S);
  or or_1 (Y, and_1_out, and_2_out);
endmodule

module mux_ocho (
  input  [7:0] O,
  input  [7:0] I,
  input  S,
  output [7:0] Y
);

  mux_cuatro mux_cuatro_1 (.A(O[3:0]), .B(I[3:0]), .S(S), .Y(Y[3:0]));
  mux_cuatro mux_cuatro_2 (.A(O[7:4]), .B(I[7:4]), .S(S), .Y(Y[7:4]));
endmodule

module mux_cuatro (
  input  [3:0] A,
  input  [3:0] B,
  input  S,
  output [3:0] Y
);

  mux_dos_bits mux_dos_bits_1 (.A(A[1:0]), .B(B[1:0]), .S(S), .Y(Y[1:0]));
  mux_dos_bits mux_dos_bits_2 (.A(A[3:2]), .B(B[3:2]), .S(S), .Y(Y[3:2]));
endmodule

module mux_dos_bits (
  input  [1:0] A,
  input  [1:0] B,
  input  S,
  output [1:0] Y
);

  mux mux_1 (.S(S), .Y(Y[0]), .O(A[0]), .I(B[0]));
  mux mux_2 (.S(S), .Y(Y[1]), .O(A[1]), .I(B[1]));

  // Notes on the sheet:
  //   AoA1
  //   B0B1
endmodule
