// Logisim project DetectorTerminado.circ as structural Verilog: 5 circuits, main circuit main
module main (
  input  in_1,
  input  in_2
);

  wire a1, a2, b1, b2, c1, c2, clock_1_out, d1, d2, e1, e2, f1, f2, g1, g2, integracion_1_s1,
       integracion_1_s2, integracion_1_s3, integracion_1_s4;
  wire [4:0] divider_1_out, divider_1_rem, integracion_1_estado_actual;

  Clock clock_1 (.out(clock_1_out));
  Integracion integracion_1 (
    .D(in_1), .Clock(clock_1_out), .Reset(in_2), .S4(integracion_1_s4), .S3(integracion_1_s3),
    .S2(integracion_1_s2), .S1(integracion_1_s1), .Estado_Actual(integracion_1_estado_actual));
  LED led_1 (.in(integracion_1_s2));
  LED led_2 (.in(integracion_1_s1));
  _7_Segment_Display u_7_segment_display_1 (.g(g1), .f(f1), .a(a1), .b(b1), .e(e1), .d(d1), .c(c1));  // open: dp
  Divider #(.width(5)) divider_1 (
    .a(integracion_1_estado_actual), .b(5'b01010), .out(divider_1_out), .rem(divider_1_rem));  // open: upper
  LED led_3 (.in(integracion_1_s4));
  LED led_4 (.in(integracion_1_s3));
  _7_Segment_Display u_7_segment_display_2 (.g(g2), .f(f2), .a(a2), .b(b2), .e(e2), .d(d2), .c(c2));  // open: dp
  BCDto7Seg bcdto7seg_1 (
    .D(divider_1_out[3]), .C(divider_1_out[2]), .B(divider_1_out[1]), .A(divider_1_out[0]), .a_2(a1),
    .b_2(b1), .c_2(c1), .d_2(d1), .e(e1), .f(f1), .g(g1));
  BCDto7Seg bcdto7seg_2 (
    .D(divider_1_rem[3]), .C(divider_1_rem[2]), .B(divider_1_rem[1]), .A(divider_1_rem[0]), .a_2(a2),
    .b_2(b2), .c_2(c2), .d_2(d2), .e(e2), .f(f2), .g(g2));

  // Notes on the sheet:
  //   S1
  //   S2
  //   S3
  //   S4
endmodule

module Salidas (
  input  Q5,
  input  Q4,
  input  Q3,
  input  Q2,
  input  Q1,
  output S4,
  output S3,
  output S2,
  output S1
);

  wire not_1_out, not_2_out, not_3_out, not_4_out, not_5_out, not_6_out, not_7_out, not_8_out;

  not not_1 (not_1_out, Q5);
  not not_2 (not_2_out, Q5);
  not not_3 (not_3_out, Q3);
  not not_4 (not_4_out, Q2);
  not not_5 (not_5_out, Q5);
  not not_6 (not_6_out, Q4);
  not not_7 (not_7_out, Q1);
  not not_8 (not_8_out, Q5);
  and and_1 (S4, not_1_out, Q4, Q3, Q2, Q1);
  and and_2 (S3, not_2_out, Q4, not_3_out, not_4_out, Q1);
  and and_3 (S2, not_5_out, not_6_out, Q3, Q2, not_7_out);
  and and_4 (S1, not_8_out, Q3, Q2, Q1);
endmodule

module FL (
  input  Q5,
  input  Q4,
  input  Q3,
  input  Q2,
  input  Q1,
  input  D,
  output J5,
  output K5,
  output J4,
  output K4,
  output J3,
  output K3,
  output J2,
  output K2,
  output J1,
  output K1
);

  wire and_2_out, and_3_out, and_4_out, and_5_out, and_6_out, and_7_out, and_8_out, and_9_out, and_10_out,
       and_11_out, and_12_out, and_13_out, and_14_out, and_15_out, and_16_out, and_17_out, and_18_out,
       and_19_out, and_20_out, and_21_out, and_22_out, and_23_out, and_24_out, and_25_out, and_26_out,
       and_27_out, and_28_out, and_29_out, and_30_out, and_31_out, and_32_out, not_1_out, not_2_out,
       not_3_out, not_4_out, not_5_out, not_6_out, not_7_out, not_8_out, not_9_out, not_10_out, not_11_out,
       not_12_out, not_13_out, not_14_out, not_15_out, not_16_out, not_17_out, not_18_out, not_19_out,
       not_20_out, not_21_out, not_22_out, not_23_out, not_24_out, not_25_out, not_26_out, not_27_out,
       not_28_out, not_29_out, not_30_out, not_31_out, not_32_out, not_33_out, not_34_out, not_35_out,
       not_36_out, not_37_out, not_38_out, not_39_out, not_40_out, not_41_out, not_42_out, not_43_out,
       not_44_out, not_45_out, not_46_out;

  not not_1 (not_1_out, Q4);
  not not_2 (not_2_out, Q3);
  not not_3 (not_3_out, D);
  not not_4 (not_4_out, Q3);
  not not_5 (not_5_out, D);
  not not_6 (not_6_out, Q2);
  not not_7 (not_7_out, Q1);
  not not_8 (not_8_out, Q1);
  not not_9 (not_9_out, D);
  not not_10 (not_10_out, Q3);
  not not_11 (not_11_out, Q2);
  not not_12 (not_12_out, Q3);
  not not_13 (not_13_out, Q1);
  not not_14 (not_14_out, D);
  not not_15 (not_15_out, Q4);
  not not_16 (not_16_out, Q1);
  not not_17 (not_17_out, D);
  not not_18 (not_18_out, Q1);
  not not_19 (not_19_out, Q4);
  not not_20 (not_20_out, Q1);
  not not_21 (not_21_out, D);
  not not_22 (not_22_out, Q4);
  not not_23 (not_23_out, Q1);
  not not_24 (not_24_out, D);
  not not_25 (not_25_out, Q1);
  not not_26 (not_26_out, Q4);
  not not_27 (not_27_out, Q3);
  not not_28 (not_28_out, D);
  not not_29 (not_29_out, Q4);
  not not_30 (not_30_out, D);
  not not_31 (not_31_out, Q3);
  not not_32 (not_32_out, Q4);
  not not_33 (not_33_out, Q3);
  not not_34 (not_34_out, Q2);
  not not_35 (not_35_out, Q4);
  not not_36 (not_36_out, Q5);
  not not_37 (not_37_out, Q3);
  not not_38 (not_38_out, D);
  not not_39 (not_39_out, Q3);
  not not_40 (not_40_out, Q2);
  not not_41 (not_41_out, Q4);
  not not_42 (not_42_out, Q3);
  not not_43 (not_43_out, Q2);
  not not_44 (not_44_out, D);
  not not_45 (not_45_out, Q2);
  not not_46 (not_46_out, D);
  and and_1 (J5, not_1_out, not_2_out, Q1, not_3_out);
  and and_2 (and_2_out, not_4_out, Q1, not_5_out);
  and and_3 (and_3_out, Q3, not_6_out, not_7_out, D);
  and and_4 (and_4_out, Q3, Q2, not_8_out, not_9_out);
  and and_5 (and_5_out, not_10_out, not_11_out, Q1);
  and and_6 (and_6_out, not_12_out, Q2, D);
  and and_7 (and_7_out, Q3, not_13_out, D);
  and and_8 (and_8_out, Q3, Q1, not_14_out);
  and and_9 (and_9_out, Q5, D);
  and and_10 (and_10_out, not_15_out, Q2, not_16_out, not_17_out);
  and and_11 (and_11_out, Q4, not_18_out, D);
  and and_12 (and_12_out, Q5, D);
  and and_13 (and_13_out, not_19_out, not_20_out, not_21_out);
  and and_14 (and_14_out, not_22_out, Q1, D);
  and and_15 (and_15_out, Q2, not_23_out, not_24_out);
  and and_16 (and_16_out, Q4, not_25_out, D);
  and and_17 (and_17_out, not_26_out, not_27_out, Q1, D);
  and and_18 (and_18_out, Q4, Q3, D);
  and and_19 (and_19_out, Q5, D);
  and and_20 (and_20_out, Q1, not_28_out);
  and and_21 (and_21_out, not_29_out, Q3, not_30_out);
  and and_22 (and_22_out, Q4, not_31_out, Q1);
  and and_23 (and_23_out, not_32_out, not_33_out, not_34_out, D);
  and and_24 (and_24_out, not_35_out, Q3, Q2, D);
  and and_25 (and_25_out, not_36_out, Q4, not_37_out, not_38_out);
  and and_26 (and_26_out, Q4, not_39_out, Q2);
  and and_27 (and_27_out, Q4, Q3, not_40_out);
  and and_28 (and_28_out, Q5, D);
  and and_29 (and_29_out, not_41_out, not_42_out, Q2);
  and and_30 (and_30_out, Q3, not_43_out, not_44_out);
  and and_31 (and_31_out, Q4, not_45_out, not_46_out);
  and and_32 (and_32_out, Q4, Q3, Q2, D);
  or or_1 (J4, and_2_out, and_3_out, and_4_out);
  or or_2 (K4, and_5_out, and_6_out, and_7_out, and_8_out, and_9_out);
  or or_3 (J3, and_10_out, and_11_out, and_12_out);
  or or_4 (K3, and_13_out, and_14_out, and_15_out, and_16_out);
  or or_5 (J2, and_17_out, and_18_out, and_19_out);
  or or_6 (K2, and_20_out, and_21_out, and_22_out);
  or or_7 (J1, and_23_out, and_24_out, and_25_out, and_26_out, and_27_out, and_28_out);
  or or_8 (K1, and_29_out, and_30_out, and_31_out, and_32_out);

  assign K5 = 1'b1;
endmodule

module Integracion (
  input  D,
  input  Clock,
  input  Reset,
  output [4:0] Estado_Actual,
  output S4,
  output S3,
  output S2,
  output S1
);

  wire fl_1_j1, fl_1_j2, fl_1_j3, fl_1_j4, fl_1_j5, fl_1_k1, fl_1_k2, fl_1_k3, fl_1_k4, fl_1_k5;

  FL fl_1 (
    .Q5(Estado_Actual[4]), .Q4(Estado_Actual[3]), .Q3(Estado_Actual[2]), .Q2(Estado_Actual[1]),
    .Q1(Estado_Actual[0]), .D(D), .J5(fl_1_j5), .K5(fl_1_k5), .J4(fl_1_j4), .K4(fl_1_k4), .J3(fl_1_j3),
    .K3(fl_1_k3), .J2(fl_1_j2), .K2(fl_1_k2), .J1(fl_1_j1), .K1(fl_1_k1));
  Salidas salidas_1 (
    .Q5(Estado_Actual[4]), .Q4(Estado_Actual[3]), .Q3(Estado_Actual[2]), .Q2(Estado_Actual[1]),
    .Q1(Estado_Actual[0]), .S4(S4), .S3(S3), .S2(S2), .S1(S1));
  J_K_Flip_Flop j_k_ff_1 (
    .J(fl_1_j5), .clk(Clock), .K(fl_1_k5), .Q(Estado_Actual[4]), .reset(Reset));  // open: Qn, preset, en
  J_K_Flip_Flop j_k_ff_2 (
    .J(fl_1_j4), .clk(Clock), .K(fl_1_k4), .Q(Estado_Actual[3]), .reset(Reset));  // open: Qn, preset, en
  J_K_Flip_Flop j_k_ff_3 (
    .J(fl_1_j3), .clk(Clock), .K(fl_1_k3), .Q(Estado_Actual[2]), .reset(Reset));  // open: Qn, preset, en
  J_K_Flip_Flop j_k_ff_4 (
    .J(fl_1_j2), .clk(Clock), .K(fl_1_k2), .Q(Estado_Actual[1]), .reset(Reset));  // open: Qn, preset, en
  J_K_Flip_Flop j_k_ff_5 (
    .J(fl_1_j1), .clk(Clock), .K(fl_1_k1), .Q(Estado_Actual[0]), .reset(Reset));  // open: Qn, preset, en
endmodule

module BCDto7Seg (
  input  D,
  input  C,
  input  B,
  input  A,
  output a_2,
  output b_2,
  output c_2,
  output d_2,
  output e,
  output f,
  output g
);

  wire and_1_out, and_2_out, and_3_out, and_4_out, and_5_out, and_6_out, and_7_out, and_8_out, and_9_out,
       and_10_out, and_11_out, and_12_out, and_13_out, and_14_out, and_15_out, and_16_out, and_17_out,
       and_18_out, not_1_out, not_2_out, not_3_out, not_4_out, not_5_out, not_6_out, not_7_out, not_8_out,
       not_9_out, not_10_out, not_11_out, not_12_out, not_13_out, not_14_out, not_15_out, not_16_out,
       not_17_out, not_18_out, not_19_out, not_20_out, not_21_out, not_22_out, or_1_out, or_2_out, or_3_out,
       or_4_out, or_7_out, or_8_out, or_9_out, or_10_out, or_13_out, or_14_out;

  not not_1 (not_1_out, C);
  and and_1 (and_1_out, not_1_out, not_2_out);
  not not_2 (not_2_out, A);
  not not_3 (not_3_out, C);
  and and_2 (and_2_out, not_3_out, B);
  and and_3 (and_3_out, C, A);
  not not_4 (not_4_out, C);
  not not_5 (not_5_out, B);
  and and_4 (and_4_out, not_5_out, not_6_out);
  not not_6 (not_6_out, A);
  not not_7 (not_7_out, B);
  or or_1 (or_1_out, not_7_out, A);
  not not_8 (not_8_out, C);
  not not_9 (not_9_out, A);
  not not_10 (not_10_out, C);
  not not_11 (not_11_out, A);
  and and_5 (and_5_out, C, not_12_out);
  not not_12 (not_12_out, B);
  not not_13 (not_13_out, C);
  and and_6 (and_6_out, not_13_out, not_14_out);
  not not_14 (not_14_out, A);
  and and_7 (and_7_out, B, not_15_out);
  not not_15 (not_15_out, A);
  not not_16 (not_16_out, B);
  and and_8 (and_8_out, not_16_out, not_17_out);
  not not_17 (not_17_out, A);
  and and_9 (and_9_out, C, not_18_out);
  not not_18 (not_18_out, B);
  and and_10 (and_10_out, C, not_19_out);
  not not_19 (not_19_out, A);
  not not_20 (not_20_out, C);
  and and_11 (and_11_out, not_20_out, B);
  and and_12 (and_12_out, C, not_21_out);
  not not_21 (not_21_out, B);
  and and_13 (and_13_out, C, not_22_out);
  not not_22 (not_22_out, A);
  or or_2 (or_2_out, and_1_out, and_2_out);
  or or_3 (or_3_out, and_3_out, D);
  or or_4 (or_4_out, not_4_out, and_4_out);
  and and_14 (and_14_out, B, A);
  or or_5 (c_2, or_1_out, C);
  and and_15 (and_15_out, not_8_out, not_9_out);
  and and_16 (and_16_out, not_10_out, B);
  and and_17 (and_17_out, B, not_11_out);
  and and_18 (and_18_out, and_5_out, A);
  or or_6 (e, and_6_out, and_7_out);
  or or_7 (or_7_out, and_8_out, and_9_out);
  or or_8 (or_8_out, and_10_out, D);
  or or_9 (or_9_out, and_11_out, and_12_out);
  or or_10 (or_10_out, and_13_out, D);
  or or_11 (a_2, or_2_out, or_3_out);
  or or_12 (b_2, or_4_out, and_14_out);
  or or_13 (or_13_out, and_15_out, and_16_out);
  or or_14 (or_14_out, and_17_out, and_18_out);
  or or_15 (f, or_7_out, or_8_out);
  or or_16 (g, or_9_out, or_10_out);
  or or_17 (d_2, or_13_out, or_14_out);
endmodule
